// Logisim project traffic_intersection.circ as structural Verilog: 8 circuits, main circuit main
module main (
  input  lights
);

  wire Btn_A_out, Btn_B_out, clk_out, GA, GB, n0, n1, n2, n3, not_1_out, not_2_out, not_3_out, not_4_out,
       not_5_out, not_6_out, o0, o1, o2, o3, o4, o5, o6, o7, o8, o9, o10, o11, o12, o13, o14, o15, p, q0, q1,
       q2, RA, RB, YA, YB;
  wire [3:0] n_2_n_1_count;

  Button Btn_A (.out(Btn_A_out));
  Button Btn_B (.out(Btn_B_out));
  Clock clk (.out(clk_out));
  Pedestrian_Buttons Pedestrian_Buttons_1 (.Btn_A(Btn_A_out), .Btn_B(Btn_B_out), .q2(q2), .p(p));
  fsm fsm_1 (.clk(clk_out), .en(1'b1), .p(p), .q0(q0), .q1(q1), .q2(q2), .n0(n0), .n1(n1), .n2(n2), .n3(n3));
  n_2_n n_2_n_1 (.n0(n0), .n1(n1), .n2(n2), .n3(n3), .q2(q2), .count(n_2_n_1_count));
  Stop_Lights Stop_Lights_1 (
    .q0(q0), .q1(q1), .q2(q2), .Red_A(RA), .Yellow_A(YA), .Green_A(GA), .Red_B(RB), .Yellow_B(YB),
    .Green_B(GB));
  Bin_2_Hex Display_1 (
    .n0(n_2_n_1_count[0]), .n1(n_2_n_1_count[1]), .n2(n_2_n_1_count[2]), .n3(n_2_n_1_count[3]), .o15(o15),
    .o14(o14), .o13(o13), .o12(o12), .o11(o11), .o10(o10), .o9(o9), .o8(o8), .o7(o7), .o6(o6), .o5(o5),
    .o4(o4), .o3(o3), .o2(o2), .o1(o1), .o0(o0));
  not not_1 (not_1_out, RA);
  LED Red_Led_A (.in(not_1_out));
  not not_2 (not_2_out, YA);
  LED Yellow_Led_A (.in(not_2_out));
  not not_3 (not_3_out, GA);
  LED Green_Led_A (.in(not_3_out));
  not not_4 (not_4_out, RB);
  LED Red_Led_B (.in(not_4_out));
  not not_5 (not_5_out, YB);
  LED Yellow_Led_B (.in(not_5_out));
  not not_6 (not_6_out, GB);
  LED Green_Led_B (.in(not_6_out));
  LED LED_1 (.in(lights));
  LED LED_2 (.in(lights));
  LED LED_3 (.in(lights));
  LED LED_4 (.in(lights));
  _7_Segment_Display left_display (.g(o14), .f(o13), .a(o8), .b(o9), .e(o12), .d(o11), .c(o10), .dp(o15));
  _7_Segment_Display right_display (.g(o6), .f(o5), .a(o0), .b(o1), .e(o4), .d(o3), .c(o2), .dp(o7));

  // Notes on the sheet:
  //   Main
endmodule

module fsm (
  input  clk,
  input  en,
  input  p,
  output q0,
  output q1,
  output q2,
  output n0,
  output n1,
  output n2,
  output n3
);

  wire and_1_out, and_2_out, and_3_out, and_4_out, and_5_out, d0, d1, d2, multiplexer_1_out,
       multiplexer_2_out, multiplexer_3_out, not_1_out, q0p, q1p, q2p, T;

  and and_1 (and_1_out, q2p, q0p);
  and and_2 (and_2_out, q2p, p, q1);
  Multiplexer multiplexer_1 (.in0(q0), .in1(d0), .out(multiplexer_1_out), .sel(T));
  Timer Timer_1 (.q2p(q2p), .q2(q2), .en(en), .clk(clk), .T(T), .n0(n0), .n1(n1), .n2(n2), .n3(n3));
  D_Flip_Flop d_ff_1 (.D(multiplexer_1_out), .clk(clk), .Q(q0), .Qn(q0p));  // open: preset, reset
  or or_1 (d0, and_1_out, and_2_out);
  Multiplexer multiplexer_2 (.in0(q1), .in1(d1), .out(multiplexer_2_out), .sel(T));
  D_Flip_Flop d_ff_2 (.D(multiplexer_2_out), .clk(clk), .Q(q1), .Qn(q1p));  // open: preset, reset
  not not_1 (not_1_out, p);
  Multiplexer multiplexer_3 (.in0(q2), .in1(d2), .out(multiplexer_3_out), .sel(T));
  and and_3 (and_3_out, q2, q1p, q0p);
  and and_4 (and_4_out, q2p, q1, q0p);
  and and_5 (and_5_out, q2p, not_1_out, q1p, q0);
  D_Flip_Flop d_ff_3 (.D(multiplexer_3_out), .clk(clk), .Q(q2), .Qn(q2p));  // open: preset, reset
  or or_2 (d1, and_3_out, and_4_out, and_5_out);
  and and_6 (d2, q2p, q0, p);

  // Notes on the sheet:
  //   fsm
endmodule

module Timer (
  input  q2p,
  input  q2,
  input  en,
  input  clk,
  output T,
  output n0,
  output n1,
  output n2,
  output n3
);

  wire and_1_out, and_2_out;

  and and_1 (and_1_out, q2p, n1);
  and and_2 (and_2_out, q2, n3, n0);
  n_register n_register_1 (
    .one(4'b0001), .en(en), .clk(clk), .T(T), .zero(4'b0000), .n0(n0), .n1(n1), .n2(n2), .n3(n3));
  or or_1 (T, and_1_out, and_2_out);

  // Notes on the sheet:
  //   Timer
endmodule

module n_register (
  input  [3:0] one,
  input  en,
  input  clk,
  input  T,
  input  [3:0] zero,
  output n0,
  output n1,
  output n2,
  output n3
);

  wire [3:0] adder_1_out, D;

  Register #(.width(4)) register_1 (.D(D), .en(en), .clk(clk), .Q({n3, n2, n1, n0}));  // open: clr
  Adder #(.width(4)) adder_1 (.a({n3, n2, n1, n0}), .b(one), .out(adder_1_out));  // open: cin, cout
  Multiplexer #(.width(4)) multiplexer_1 (.in0(adder_1_out), .in1(zero), .out(D), .sel(T));

  // Other names for the same wires on the sheet: Q[3:0] = {n3, n2, n1, n0}

  // Notes on the sheet:
  //   n register
endmodule

module Stop_Lights (
  input  q0,
  input  q1,
  input  q2,
  output Red_A,
  output Yellow_A,
  output Green_A,
  output Red_B,
  output Yellow_B,
  output Green_B
);

  wire not_1_out, not_2_out, not_3_out, not_4_out, not_5_out, not_6_out, not_7_out, not_8_out, not_9_out;

  not not_1 (not_1_out, q2);
  not not_2 (not_2_out, q1);
  not not_3 (not_3_out, q2);
  not not_4 (not_4_out, q1);
  not not_5 (not_5_out, q0);
  not not_6 (not_6_out, q1);
  not not_7 (not_7_out, q2);
  not not_8 (not_8_out, q2);
  not not_9 (not_9_out, q0);
  or or_1 (Red_A, q2, q1);
  and and_1 (Yellow_A, not_1_out, not_2_out, q0);
  and and_2 (Green_A, not_3_out, not_4_out, not_5_out);
  or or_2 (Red_B, q2, not_6_out);
  and and_3 (Yellow_B, not_7_out, q1, q0);
  and and_4 (Green_B, not_8_out, q1, not_9_out);

  // Other names for the same wires on the sheet: GA = Green_A; GB = Green_B; RA = Red_A; RB = Red_B; YA = Yellow_A;
  //   YB = Yellow_B

  // Notes on the sheet:
  //   Stop Lights
endmodule

module Pedestrian_Buttons (
  input  Btn_A,
  input  Btn_B,
  input  q2,
  output p
);

  wire not_1_out, or_1_out, set;

  or or_1 (or_1_out, Btn_A, Btn_B);
  not not_1 (not_1_out, q2);
  and and_1 (set, or_1_out, not_1_out);
  D_Flip_Flop d_ff_1 (.D(1'b0), .clk(1'b0), .Q(p), .preset(set), .reset(q2));  // open: Qn

  // Notes on the sheet:
  //   Pedestrian Buttons
endmodule

module Bin_2_Hex (
  input  n0,
  input  n1,
  input  n2,
  input  n3,
  output o15,
  output o14,
  output o13,
  output o12,
  output o11,
  output o10,
  output o9,
  output o8,
  output o7,
  output o6,
  output o5,
  output o4,
  output o3,
  output o2,
  output o1,
  output o0
);

  wire and_1_out, and_2_out, and_3_out, and_4_out, and_5_out, and_6_out, and_7_out, and_8_out, and_9_out,
       and_10_out, and_11_out, and_12_out, and_13_out, and_14_out, and_15_out, and_16_out, and_17_out,
       and_18_out, not_1_out, not_2_out, not_3_out, not_4_out, not_5_out, not_6_out, not_7_out, not_8_out,
       not_9_out, not_10_out, not_11_out, not_12_out, not_13_out, not_14_out, not_15_out, not_16_out,
       not_17_out, not_18_out, not_19_out, not_20_out, not_21_out, not_22_out, not_23_out, not_24_out,
       not_25_out, not_26_out, not_27_out, not_28_out, not_29_out, not_30_out, not_31_out, not_32_out,
       not_33_out, not_34_out, not_35_out, not_36_out;

  not not_1 (not_1_out, n3);
  not not_2 (not_2_out, n1);
  not not_3 (not_3_out, n3);
  not not_4 (not_4_out, n1);
  not not_5 (not_5_out, n3);
  not not_6 (not_6_out, n1);
  not not_7 (not_7_out, n3);
  not not_8 (not_8_out, n1);
  or or_1 (o13, not_1_out, not_2_out);
  or or_2 (o12, not_3_out, not_4_out);
  or or_3 (o11, not_5_out, not_6_out);
  or or_4 (o8, not_7_out, not_8_out);
  not not_9 (not_9_out, n1);
  not not_10 (not_10_out, n1);
  not not_11 (not_11_out, n0);
  not not_12 (not_12_out, n3);
  not not_13 (not_13_out, n2);
  not not_14 (not_14_out, n3);
  not not_15 (not_15_out, n0);
  not not_16 (not_16_out, n2);
  not not_17 (not_17_out, n1);
  not not_18 (not_18_out, n0);
  not not_19 (not_19_out, n1);
  and and_1 (and_1_out, n3, not_9_out);
  and and_2 (and_2_out, n2, not_10_out);
  and and_3 (and_3_out, not_12_out, n1, not_13_out);
  and and_4 (and_4_out, not_14_out, n1, not_15_out);
  and and_5 (and_5_out, n1, not_11_out);
  and and_6 (and_6_out, not_16_out, not_17_out, not_18_out);
  or or_5 (o2, not_19_out, n0, n2, n3);
  or or_6 (o6, and_1_out, and_2_out, and_3_out, and_4_out);
  not not_20 (not_20_out, n2);
  not not_21 (not_21_out, n2);
  not not_22 (not_22_out, n1);
  not not_23 (not_23_out, n0);
  or or_7 (o4, and_5_out, and_6_out);
  and and_7 (and_7_out, n2, n0);
  and and_8 (and_8_out, not_20_out, n1);
  and and_9 (and_9_out, not_21_out, not_22_out, not_23_out);
  not not_24 (not_24_out, n0);
  not not_25 (not_25_out, n1);
  not not_26 (not_26_out, n1);
  not not_27 (not_27_out, n0);
  not not_28 (not_28_out, n0);
  not not_29 (not_29_out, n2);
  not not_30 (not_30_out, n1);
  not not_31 (not_31_out, n1);
  not not_32 (not_32_out, n0);
  or or_8 (o0, n3, and_7_out, and_8_out, and_9_out);
  and and_10 (and_10_out, not_24_out, not_25_out);
  and and_11 (and_11_out, n2, not_26_out);
  and and_12 (and_12_out, n2, not_27_out);
  and and_13 (and_13_out, not_28_out, n1);
  not not_33 (not_33_out, n2);
  not not_34 (not_34_out, n0);
  not not_35 (not_35_out, n1);
  and and_14 (and_14_out, not_31_out, not_32_out);
  and and_15 (and_15_out, n1, n0);
  and and_16 (and_16_out, not_29_out, n1);
  and and_17 (and_17_out, not_33_out, not_30_out, not_34_out);
  and and_18 (and_18_out, n2, not_35_out, n0);
  not not_36 (not_36_out, n2);
  or or_9 (o5, n3, and_10_out, and_11_out, and_12_out);
  or or_10 (o1, not_36_out, n3, and_14_out, and_15_out);
  or or_11 (o3, and_13_out, and_16_out, and_17_out, and_18_out);

  assign o7 = 1'b0;
  assign o9 = 1'b1;
  assign o10 = 1'b1;
  assign o14 = 1'b0;
  assign o15 = 1'b0;

  // Notes on the sheet:
  //   Bin to Hex
endmodule

module n_2_n (
  input  n0,
  input  n1,
  input  n2,
  input  n3,
  input  q2,
  output [3:0] count
);

  wire and_1_out, and_2_out, and_3_out, and_4_out, and_5_out, and_6_out, and_7_out, not_1_out, not_2_out,
       not_3_out, not_4_out, not_5_out, not_6_out, not_7_out, not_8_out, not_9_out, not_10_out;
  wire [1:0] not_12_out;
  wire [3:1] or_3_out;

  not not_1 (not_1_out, n3);
  not not_2 (not_2_out, n2);
  not not_3 (not_3_out, n1);
  not not_4 (not_4_out, n2);
  not not_5 (not_5_out, n0);
  not not_6 (not_6_out, n1);
  not not_7 (not_7_out, n0);
  not not_8 (not_8_out, n1);
  not not_9 (not_9_out, n0);
  not not_10 (not_10_out, n2);
  and and_1 (and_1_out, n2, not_8_out);
  and and_2 (and_2_out, n2, not_9_out);
  and and_3 (and_3_out, not_10_out, n1, n0);
  not not_11 (not_12_out[1], n1);
  not not_12 (not_12_out[0], n0);
  and and_4 (and_4_out, not_1_out, not_2_out, not_3_out);
  and and_5 (and_5_out, not_4_out, n1, not_5_out);
  and and_6 (and_6_out, not_6_out, not_7_out);
  and and_7 (and_7_out, n1, n0);
  or or_1 (or_3_out[3], and_4_out, and_5_out);
  or or_2 (or_3_out[2], and_1_out, and_2_out, and_3_out);
  or or_3 (or_3_out[1], and_6_out, and_7_out);
  Multiplexer #(.width(4)) multiplexer_1 (.in0({2'b00, not_12_out}), .in1({or_3_out, n0}), .out(count), .sel(q2));

  // Notes on the sheet:
  //   N count Converter
endmodule
